// Logisim project D_reg.circ as structural Verilog: 21 circuits, main circuit D_reg
module D_reg (
  input  WE,
  input  D,
  output Q,
  output Qn
);

  wire and_1_out, and_2_out, not_1_out;

  not not_1 (not_1_out, D);
  and and_1 (and_1_out, not_1_out, WE);
  and and_2 (and_2_out, WE, D);
  nor nor_1 (Q, and_1_out, Qn);
  nor nor_2 (Qn, Q, and_2_out);
endmodule

module D_Flip_Flop (
  input  CLK,
  input  D,
  output Q,
  output Qn
);

  wire d_reg_1_q, not_1_out;

  not not_1 (not_1_out, CLK);
  D_reg d_reg_1 (.WE(not_1_out), .D(D), .Q(d_reg_1_q));  // open: Qn
  D_reg d_reg_2 (.WE(CLK), .D(d_reg_1_q), .Q(Q), .Qn(Qn));
endmodule

module D_reg_rst (
  input  RST,
  input  WE,
  input  D,
  output out_4,
  output out_5
);

  wire and_1_out, not_1_out, or_1_out;

  not not_1 (not_1_out, RST);
  or or_1 (or_1_out, RST, WE);
  and and_1 (and_1_out, not_1_out, D);
  D_reg d_reg_1 (.WE(or_1_out), .D(and_1_out), .Q(out_4), .Qn(out_5));
endmodule

module D_Flip_Flop_rst (
  input  RST,
  input  CLK,
  input  D,
  output Q
);

  wire d_reg_rst_1_out_4, not_1_out;

  not not_1 (not_1_out, CLK);
  D_reg_rst d_reg_rst_1 (.RST(RST), .WE(not_1_out), .D(D), .out_4(d_reg_rst_1_out_4));  // open: out_5
  D_reg_rst d_reg_rst_2 (.RST(RST), .WE(CLK), .D(d_reg_rst_1_out_4), .out_4(Q));  // open: out_5
endmodule

module Loop_Test (
  input  in_1,
  input  in_2
);

  wire d_flip_flop_rst_1_q, not_1_out;

  D_Flip_Flop_rst d_flip_flop_rst_1 (.RST(in_1), .CLK(in_2), .D(not_1_out), .Q(d_flip_flop_rst_1_q));
  not not_1 (not_1_out, d_flip_flop_rst_1_q);
endmodule

module D_Flip_Flop_neg (
  input  CLK,
  input  D,
  output out_3
);

  wire d_reg_1_q, not_1_out;

  not not_1 (not_1_out, CLK);
  D_reg d_reg_1 (.WE(CLK), .D(D), .Q(d_reg_1_q));  // open: Qn
  D_reg d_reg_2 (.WE(not_1_out), .D(d_reg_1_q), .Q(out_3));  // open: Qn
endmodule

module D_Flip_Flop_new (
  input  in_1,
  input  in_2,
  output out_3,
  output out_4
);

  wire nand_1_out, nand_2_out, nand_3_out, nand_4_out;

  nand nand_1 (nand_1_out, nand_4_out, nand_2_out);
  nand nand_2 (nand_2_out, nand_1_out, in_1);
  nand nand_3 (nand_3_out, nand_2_out, in_1, nand_4_out);
  nand nand_4 (nand_4_out, nand_3_out, in_2);
  nand nand_5 (out_3, nand_2_out, out_4);
  nand nand_6 (out_4, out_3, nand_3_out);
endmodule

module D_Flip_Flop_En (
  input  EN,
  input  CLK,
  input  D,
  output out_4,
  output out_5
);

  wire not_1_out, or_1_out;

  not not_1 (not_1_out, EN);
  or or_1 (or_1_out, not_1_out, CLK);
  D_Flip_Flop d_flip_flop_1 (.CLK(or_1_out), .D(D), .Q(out_4), .Qn(out_5));
endmodule

module Half_Adder (
  input  A,
  input  B,
  output S,
  output C
);

  xor xor_1 (S, A, B);
  and and_1 (C, A, B);
endmodule

module Full_Adder (
  input  A,
  input  B,
  input  Cin,
  output Cout,
  output S
);

  wire half_adder_1_c, half_adder_1_s, half_adder_2_c;

  Half_Adder half_adder_1 (.A(A), .B(B), .S(half_adder_1_s), .C(half_adder_1_c));
  Half_Adder half_adder_2 (.A(half_adder_1_s), .B(Cin), .S(S), .C(half_adder_2_c));
  or or_1 (Cout, half_adder_1_c, half_adder_2_c);
endmodule

module Full_Adder_4 (
  input  Cin,
  input  [3:0] A,
  input  [3:0] B,
  output [3:0] S,
  output Cout
);

  wire full_adder_1_cout, full_adder_2_cout, full_adder_3_cout;

  Full_Adder full_adder_1 (.A(A[0]), .B(B[0]), .Cin(Cin), .Cout(full_adder_1_cout), .S(S[0]));
  Full_Adder full_adder_2 (.A(A[1]), .B(B[1]), .Cin(full_adder_1_cout), .Cout(full_adder_2_cout), .S(S[1]));
  Full_Adder full_adder_3 (.A(A[2]), .B(B[2]), .Cin(full_adder_2_cout), .Cout(full_adder_3_cout), .S(S[2]));
  Full_Adder full_adder_4 (.A(A[3]), .B(B[3]), .Cin(full_adder_3_cout), .Cout(Cout), .S(S[3]));
endmodule

module DFF (
  input  RST,
  input  CLK,
  input  D,
  input  EN,
  output out_5,
  output Q
);

  wire d_reg_rst_1_out_4, not_1_out, not_2_out, or_1_out;

  not not_1 (not_1_out, EN);
  or or_1 (or_1_out, CLK, not_1_out);
  not not_2 (not_2_out, or_1_out);
  D_reg_rst d_reg_rst_1 (.RST(RST), .WE(not_2_out), .D(D), .out_4(d_reg_rst_1_out_4));  // open: out_5
  D_reg_rst d_reg_rst_2 (.RST(RST), .WE(or_1_out), .D(d_reg_rst_1_out_4), .out_4(out_5));  // open: out_5
endmodule

module REG4 (
  input  RST,
  input  CLK,
  input  EN,
  input  [3:0] D,
  output [3:0] Q
);

  DFF dff_1 (.RST(RST), .CLK(CLK), .D(D[0]), .EN(EN), .out_5(Q[0]));  // open: Q
  DFF dff_2 (.RST(RST), .CLK(CLK), .D(D[1]), .EN(EN), .out_5(Q[1]));  // open: Q
  DFF dff_3 (.RST(RST), .CLK(CLK), .D(D[2]), .EN(EN), .out_5(Q[2]));  // open: Q
  DFF dff_4 (.RST(RST), .CLK(CLK), .D(D[3]), .EN(EN), .out_5(Q[3]));  // open: Q
endmodule

module CNT4 (
  input  [3:0] Max,
  input  RST,
  input  CLK,
  input  EN,
  output [3:0] CNT,
  output FULL
);

  wire [3:0] full_adder_4_1_s, multiplexer_1_out, xnor_1_out;

  // Probe on multiplexer_1_out
  Hex_Digit_Display hex_digit_display_1 (.value(CNT));  // open: dp
  REG4 reg4_1 (.RST(RST), .CLK(CLK), .EN(EN), .D(multiplexer_1_out), .Q(CNT));
  // Probe on CNT
  Multiplexer #(.width(4)) multiplexer_1 (.in0(full_adder_4_1_s), .in1(4'b0000), .out(multiplexer_1_out), .sel(FULL));
  Full_Adder_4 full_adder_4_1 (.Cin(1'b1), .A(CNT), .B(4'b0000), .S(full_adder_4_1_s));  // open: Cout
  assign xnor_1_out = ~(Max ^ CNT);  // XNOR_Gate xnor_1, 4 bits wide
  and and_1 (FULL, xnor_1_out[0], xnor_1_out[1], xnor_1_out[2], xnor_1_out[3]);
endmodule

module Add_From_1_to_10 (
  input  RST,
  input  [3:0] in_2,
  output [7:0] out_3
);

  wire clock_1_out, nand_1_out;
  wire [3:0] cnt4_1_cnt, xnor_1_out;
  wire [7:0] add8_1_s;

  Clock clock_1 (.out(clock_1_out));
  CNT4 cnt4_1 (.Max(4'b1111), .RST(RST), .CLK(clock_1_out), .EN(nand_1_out), .CNT(cnt4_1_cnt));  // open: FULL
  // Probe on cnt4_1_cnt
  // Probe on in_2
  // Probe on cnt4_1_cnt
  assign xnor_1_out = ~(cnt4_1_cnt ^ in_2);  // XNOR_Gate xnor_1, 4 bits wide
  nand nand_1 (nand_1_out, xnor_1_out[0], xnor_1_out[1], xnor_1_out[2], xnor_1_out[3]);
  ADD8 add8_1 (.Cin(1'b0), .A({4'b0000, cnt4_1_cnt}), .B(out_3), .S(add8_1_s));  // open: Cout
  REG8 reg8_1 (.RST(RST), .CLK(clock_1_out), .EN(nand_1_out), .D(add8_1_s), .Q(out_3));

  // Notes on the sheet:
  //   in_2: initial=0xb
endmodule

module REG8 (
  input  RST,
  input  CLK,
  input  EN,
  input  [7:0] D,
  output [7:0] Q
);

  REG4 reg4_1 (.RST(RST), .CLK(CLK), .EN(EN), .D(D[3:0]), .Q(Q[3:0]));
  REG4 reg4_2 (.RST(RST), .CLK(CLK), .EN(EN), .D(D[7:4]), .Q(Q[7:4]));
endmodule

module ADD8 (
  input  Cin,
  input  [7:0] A,
  input  [7:0] B,
  output [7:0] S,
  output Cout
);

  wire full_adder_4_1_cout;

  Full_Adder_4 full_adder_4_1 (.Cin(Cin), .A(A[3:0]), .B(B[3:0]), .S(S[3:0]), .Cout(full_adder_4_1_cout));
  Full_Adder_4 full_adder_4_2 (.Cin(full_adder_4_1_cout), .A(A[7:4]), .B(B[7:4]), .S(S[7:4]), .Cout(Cout));
endmodule

module Watch (
  input  in_1
);

  wire and_1_out, and_2_out, clock_1_out, cnt4_1_full, cnt4_2_full, cnt4_3_full;
  wire [3:0] cnt4_1_cnt, cnt4_2_cnt, cnt4_3_cnt, cnt4_4_cnt;

  Clock clock_1 (.out(clock_1_out));
  CNT4 cnt4_1 (.Max(4'b1001), .RST(in_1), .CLK(clock_1_out), .EN(1'b1), .CNT(cnt4_1_cnt), .FULL(cnt4_1_full));
  CNT4 cnt4_2 (.Max(4'b0101), .RST(in_1), .CLK(clock_1_out), .EN(cnt4_1_full), .CNT(cnt4_2_cnt), .FULL(cnt4_2_full));
  and and_1 (and_1_out, cnt4_2_full, cnt4_1_full);
  CNT4 cnt4_3 (.Max(4'b1001), .RST(in_1), .CLK(clock_1_out), .EN(and_1_out), .CNT(cnt4_3_cnt), .FULL(cnt4_3_full));
  and and_2 (and_2_out, cnt4_3_full, cnt4_2_full, cnt4_1_full);
  CNT4 cnt4_4 (.Max(4'b0101), .RST(in_1), .CLK(clock_1_out), .EN(and_2_out), .CNT(cnt4_4_cnt));  // open: FULL
  Hex_Digit_Display hex_digit_display_1 (.value(cnt4_3_cnt));  // open: dp
  Hex_Digit_Display hex_digit_display_2 (.value(cnt4_4_cnt));  // open: dp
  Hex_Digit_Display hex_digit_display_3 (.value(cnt4_2_cnt));  // open: dp
  Hex_Digit_Display hex_digit_display_4 (.value(cnt4_1_cnt));  // open: dp
endmodule

module DIY_ROM (
  input  [3:0] PC,
  output [7:0] ins
);

  Multiplexer #(.select(4), .width(8)) multiplexer_1 (
    .in0(8'h8b), .in1(8'h91), .in2(8'ha0), .in3(8'hb2), .in4(8'h26), .in5(8'h17), .in6(8'hd1), .in7(8'h42),
    .in8(8'he3), .in9({8{1'b1}}), .in10({8{1'b1}}), .in11({8{1'b1}}), .in12({8{1'b1}}), .in13({8{1'b1}}),
    .in14({8{1'b1}}), .in15({8{1'b1}}), .out(ins), .sel(PC));
endmodule

module DIY_RAM (
  input  clk,
  input  [7:0] wdata,
  input  [1:0] raddr1,
  input  wen,
  input  [1:0] raddr2,
  input  [1:0] waddr,
  output [7:0] rdata1,
  output [7:0] rdata2
);

  wire and_1_out, and_2_out, and_3_out, and_4_out, decoder_1_out0, decoder_1_out1, decoder_1_out2,
       decoder_1_out3;
  wire [7:0] register_1_q, register_2_q, register_3_q, register_4_q;

  Decoder #(.enable("false"), .select(2)) decoder_1 (
    .out0(decoder_1_out0), .out1(decoder_1_out1), .out2(decoder_1_out2), .out3(decoder_1_out3), .sel(waddr));
  and and_1 (and_1_out, wen, decoder_1_out0);
  and and_2 (and_2_out, wen, decoder_1_out1);
  and and_3 (and_3_out, wen, decoder_1_out2);
  and and_4 (and_4_out, wen, decoder_1_out3);
  Register register_1 (.D(wdata), .en(and_1_out), .clk(clk), .Q(register_1_q));  // open: clr
  Register register_2 (.D(wdata), .en(and_2_out), .clk(clk), .Q(register_2_q));  // open: clr
  Register register_3 (.D(wdata), .en(and_3_out), .clk(clk), .Q(register_3_q));  // open: clr
  Register register_4 (.D(wdata), .en(and_4_out), .clk(clk), .Q(register_4_q));  // open: clr
  Multiplexer #(.select(2), .width(8)) multiplexer_1 (
    .in0(register_1_q), .in1(register_2_q), .in2(register_3_q), .in3(register_4_q), .out(rdata1), .sel(raddr1));
  Multiplexer #(.select(2), .width(8)) multiplexer_2 (
    .in0(register_1_q), .in1(register_2_q), .in2(register_3_q), .in3(register_4_q), .out(rdata2), .sel(raddr2));
endmodule

module DIY_CORE (
  input  in_1
);

  wire clock_1_out, comparator_1_eq, decoder_1_out0, decoder_1_out1, decoder_1_out2, decoder_1_out3,
       not_1_out, or_1_out, or_2_out;
  wire [1:0] multiplexer_2_out;
  wire [3:0] full_adder_4_1_s, multiplexer_3_out, reg4_1_q;
  wire [7:0] add8_1_s, diy_ram_1_rdata1, diy_ram_1_rdata2, diy_rom_1_ins, multiplexer_1_out, reg8_1_q;

  Clock clock_1 (.out(clock_1_out));
  DIY_ROM diy_rom_1 (.PC(reg4_1_q), .ins(diy_rom_1_ins));
  // Probe on diy_rom_1_ins
  Decoder #(.enable("false"), .select(2)) decoder_1 (
    .out0(decoder_1_out0), .out1(decoder_1_out1), .out2(decoder_1_out2), .out3(decoder_1_out3),
    .sel(diy_rom_1_ins[7:6]));
  or or_1 (or_1_out, decoder_1_out0, decoder_1_out2);
  // Probe on multiplexer_3_out
  Multiplexer #(.width(8)) multiplexer_1 (
    .in0(add8_1_s), .in1({4'b0000, diy_rom_1_ins[3:0]}), .out(multiplexer_1_out), .sel(decoder_1_out2));
  // Probe on multiplexer_1_out
  Multiplexer #(.width(2)) multiplexer_2 (
    .in0(diy_rom_1_ins[3:2]), .in1(2'b00), .out(multiplexer_2_out), .sel(decoder_1_out3));
  // Probe on diy_rom_1_ins[5:4]
  REG4 reg4_1 (.RST(in_1), .CLK(clock_1_out), .EN(1'b1), .D(multiplexer_3_out), .Q(reg4_1_q));
  Multiplexer #(.width(4)) multiplexer_3 (
    .in0(diy_rom_1_ins[5:2]), .in1(full_adder_4_1_s), .out(multiplexer_3_out), .sel(or_2_out));
  REG8 reg8_1 (.RST(in_1), .CLK(clock_1_out), .EN(decoder_1_out1), .D(diy_ram_1_rdata2), .Q(reg8_1_q));
  // Probe on reg4_1_q
  Hex_Digit_Display hex_digit_display_1 (.value(reg8_1_q[7:4]));  // open: dp
  Hex_Digit_Display hex_digit_display_2 (.value(reg8_1_q[3:0]));  // open: dp
  DIY_RAM diy_ram_1 (
    .clk(clock_1_out), .wdata(multiplexer_1_out), .raddr1(multiplexer_2_out), .wen(or_1_out),
    .raddr2(diy_rom_1_ins[1:0]), .waddr(diy_rom_1_ins[5:4]), .rdata1(diy_ram_1_rdata1),
    .rdata2(diy_ram_1_rdata2));
  not not_1 (not_1_out, decoder_1_out3);
  Full_Adder_4 full_adder_4_1 (.Cin(1'b1), .A(reg4_1_q), .S(full_adder_4_1_s));  // open: B, Cout
  Comparator comparator_1 (.a(diy_ram_1_rdata1), .b(diy_ram_1_rdata2), .eq(comparator_1_eq));  // open: gt, lt
  ADD8 add8_1 (.A(diy_ram_1_rdata1), .B(diy_ram_1_rdata2), .S(add8_1_s));  // open: Cin, Cout
  or or_2 (or_2_out, comparator_1_eq, not_1_out);

  // Notes on the sheet:
  //   out: 01|xxxx|rs2
endmodule
