// Logisim project D_reg_rst.circ as structural Verilog: 2 circuits, main circuit main
module main (
  input  WE,
  input  RST,
  input  D,
  output Q,
  output Qn
);

  wire and_1_out, and_2_out, and_3_out, not_1_out, not_2_out, or_1_out;

  not not_1 (not_1_out, RST);
  or or_1 (or_1_out, RST, WE);
  and and_1 (and_1_out, not_1_out, D);
  not not_2 (not_2_out, and_1_out);
  and and_2 (and_2_out, not_2_out, or_1_out);
  and and_3 (and_3_out, or_1_out, and_1_out);
  nor nor_1 (Q, and_2_out, Qn);
  nor nor_2 (Qn, Q, and_3_out);
endmodule

module test (
  input  in_1,
  input  in_2
);

  wire main_1_q, not_1_out;

  main main_1 (.WE(in_1), .RST(in_2), .D(not_1_out), .Q(main_1_q));  // open: Qn
  not not_1 (not_1_out, main_1_q);
endmodule
