// Logisim project SR_reg_n.circ as structural Verilog: 1 circuit, main circuit main
module main (
  input  R,
  input  S,
  output Q,
  output Qn
);

  nand nand_1 (Q, R, Qn);
  nand nand_2 (Qn, Q, S);
endmodule
