// Logisim project ans_2_4decoder.circ as structural Verilog
module TwoFourDecoder (
  input  A0,
  input  A1,
  output Y0,
  output Y1,
  output Y2,
  output Y3
);

  wire not_1_out, not_2_out;

  not not_1 (not_1_out, A0);
  not not_2 (not_2_out, A1);
  and and_1 (Y0, not_1_out, not_2_out);
  and and_2 (Y1, A0, not_2_out);
  and and_3 (Y2, not_1_out, A1);
  and and_4 (Y3, A0, A1);
endmodule

module ThreeEightDecoder (
  input  A0,
  input  A1,
  input  A2,
  output Y0,
  output Y1,
  output Y2,
  output Y3,
  output Y4,
  output Y5,
  output Y6,
  output Y7
);

  wire [3:0] not_1_out, twofourdecoder_1_y0, twofourdecoder_2_y0;

  TwoFourDecoder twofourdecoder_1 (
    .A0(A0), .A1(A1), .Y0(twofourdecoder_1_y0[0]), .Y1(twofourdecoder_1_y0[1]), .Y2(twofourdecoder_1_y0[2]),
    .Y3(twofourdecoder_1_y0[3]));
  TwoFourDecoder twofourdecoder_2 (
    .A0(A0), .A1(A1), .Y0(twofourdecoder_2_y0[0]), .Y1(twofourdecoder_2_y0[1]), .Y2(twofourdecoder_2_y0[2]),
    .Y3(twofourdecoder_2_y0[3]));
  assign not_1_out = ~{4{A2}};  // NOT_Gate not_1, 4 bits wide
  assign {Y3, Y2, Y1, Y0} = twofourdecoder_1_y0 & not_1_out;  // AND_Gate and_1, 4 bits wide
  assign {Y7, Y6, Y5, Y4} = twofourdecoder_2_y0 & {4{A2}};  // AND_Gate and_2, 4 bits wide
endmodule

module Segment (
  input  [3:0] in_1
);

  wire decoder_1_out0, decoder_1_out1, decoder_1_out2, decoder_1_out3, decoder_1_out4, decoder_1_out5,
       decoder_1_out6, decoder_1_out7, decoder_1_out8, decoder_1_out9, decoder_1_out10, decoder_1_out11,
       decoder_1_out12, decoder_1_out13, decoder_1_out14, decoder_1_out15, nor_1_out, nor_2_out, nor_3_out,
       nor_4_out, nor_5_out, nor_6_out, nor_7_out;

  Decoder #(.select(4)) decoder_1 (
    .out0(decoder_1_out0), .out1(decoder_1_out1), .out2(decoder_1_out2), .out3(decoder_1_out3),
    .out4(decoder_1_out4), .out5(decoder_1_out5), .out6(decoder_1_out6), .out7(decoder_1_out7),
    .out8(decoder_1_out8), .out9(decoder_1_out9), .out10(decoder_1_out10), .out11(decoder_1_out11),
    .out12(decoder_1_out12), .out13(decoder_1_out13), .out14(decoder_1_out14), .out15(decoder_1_out15),
    .sel(in_1));  // open: en
  nor nor_1 (nor_1_out, decoder_1_out1, decoder_1_out4, decoder_1_out7, decoder_1_out10, decoder_1_out15);
  nor nor_2 (nor_2_out, decoder_1_out2, decoder_1_out12, decoder_1_out14, decoder_1_out15);
  nor nor_3 (nor_3_out, decoder_1_out1, decoder_1_out3, decoder_1_out4, decoder_1_out5, decoder_1_out7, decoder_1_out9);
  nor nor_4 (nor_4_out, decoder_1_out5, decoder_1_out6, decoder_1_out11, decoder_1_out12, decoder_1_out14, decoder_1_out15);
  nor nor_5 (nor_5_out, decoder_1_out1, decoder_1_out2, decoder_1_out3, decoder_1_out7, decoder_1_out13);
  nor nor_6 (nor_6_out, decoder_1_out1, decoder_1_out4, decoder_1_out11, decoder_1_out13);
  nor nor_7 (nor_7_out, decoder_1_out0, decoder_1_out1, decoder_1_out7, decoder_1_out12);
  _7_Segment_Display u_7_segment_display_1 (
    .g(nor_7_out), .f(nor_5_out), .a(nor_6_out), .b(nor_4_out), .e(nor_3_out), .d(nor_1_out), .c(nor_2_out));  // open: dp
endmodule
