// Logisim project ans_mux.circ as structural Verilog
module SingleBitMux (
  input  S,
  input  D0,
  input  D1,
  output Y
);

  wire and_1_out, and_2_out, not_1_out;

  not not_1 (not_1_out, S);
  and and_1 (and_1_out, not_1_out, D0);
  and and_2 (and_2_out, S, D1);
  or or_1 (Y, and_1_out, and_2_out);
endmodule

module Mux2 (
  input  S0,
  input  S1,
  input  D0,
  input  D1,
  input  D2,
  input  D3,
  output Y
);

  wire singlebitmux_1_y, singlebitmux_2_y;

  SingleBitMux singlebitmux_1 (.S(S0), .D0(D0), .D1(D1), .Y(singlebitmux_1_y));
  SingleBitMux singlebitmux_2 (.S(S0), .D0(D2), .D1(D3), .Y(singlebitmux_2_y));
  SingleBitMux singlebitmux_3 (.S(S1), .D0(singlebitmux_1_y), .D1(singlebitmux_2_y), .Y(Y));
endmodule
